# Fritzing sketch GO_CORONA_SHIELD (saved by Fritzing 0.9.4)
breadboards: 1

parts:
  Part1 = Arduino Nano (Rev3.0)
  J1 = Piezo Speaker
  Grove1 = Grove OLED 128x96
  J2 = Infrared Proximity Sensor
  LED1 = LED - 5mm [color="Red (633nm)" package="5 mm [THT]"]
  R1 = Resistor [tolerance=±5% resistance=220 package="2010 [SMD]"]
  T1 = LM35 Temperature Sensor [package="TO92 [THT]"]

nets:
  GND: Part1.GND, J1.pin1, Grove1.GND, J2.GND, R1.Pin_0, T1.GND
  N1: Part1.D5, J1.pin2
  N2: Part1.D6, LED1.anode
  N3: Part1.D7, J2.Vout
  VCC: Part1.5V, Grove1.VCC, J2.Vcc, T1.+Vs
  N4: Part1.A5, Grove1.SCL
  N5: Part1.A4, Grove1.SDA
  N6: Part1.A0, T1.Vout
  N7: LED1.cathode, R1.Pin_1

// code stored in the sketch: GO_CORONA.ino

